// Logisim project CRC检验.circ as structural Verilog: 3 circuits, main circuit CRC
module CRC (
  input  [7:0] in_1,
  input  [3:0] in_2,
  output [10:0] out_3
);

  \_4位模二除法器  \u_4位模二除法器_1  (.in_1(in_1), .in_2(in_2), .out_3(out_3[2:0]));

  assign out_3[10:3] = in_1;
endmodule

module \_4位模二除法器  (
  input  [7:0] in_1,
  input  [3:0] in_2,
  output [2:0] out_3
);

  wire [2:0] basic_1_out_3, basic_2_out_3, basic_3_out_3, basic_4_out_3, basic_5_out_3, basic_6_out_3,
       basic_7_out_3;

  basic basic_1 (.\被除数 (in_1[7:4]), .\除数 (in_2), .out_3(basic_1_out_3));
  basic basic_2 (.\被除数 ({basic_1_out_3, in_1[3]}), .\除数 (in_2), .out_3(basic_2_out_3));
  basic basic_3 (.\被除数 ({basic_2_out_3, in_1[2]}), .\除数 (in_2), .out_3(basic_3_out_3));
  basic basic_4 (.\被除数 ({basic_3_out_3, in_1[1]}), .\除数 (in_2), .out_3(basic_4_out_3));
  basic basic_5 (.\被除数 ({basic_4_out_3, in_1[0]}), .\除数 (in_2), .out_3(basic_5_out_3));
  basic basic_6 (.\被除数 ({basic_5_out_3, 1'b0}), .\除数 (in_2), .out_3(basic_6_out_3));
  basic basic_7 (.\被除数 ({basic_6_out_3, 1'b0}), .\除数 (in_2), .out_3(basic_7_out_3));
  basic basic_8 (.\被除数 ({basic_7_out_3, 1'b0}), .\除数 (in_2), .out_3(out_3));
endmodule

module basic (
  input  [3:0] \被除数 ,
  input  [3:0] \除数 ,
  output [2:0] out_3
);

  wire [2:0] xor_2_out;

  xor xor_1 (xor_2_out[2], \被除数 [2], \除数 [2]);
  xor xor_2 (xor_2_out[0], \被除数 [0], \除数 [0]);
  xor xor_3 (xor_2_out[1], \被除数 [1], \除数 [1]);
  Multiplexer #(.width(3), .disabled(0), .enable("false")) multiplexer_1 (
    .in0(\被除数 [2:0]), .in1(xor_2_out), .out(out_3), .sel(\被除数 [3]));
endmodule
