// Logisim project fsm.circ as structural Verilog: 4 circuits, main circuit fsm
module fsm (
  input  CLR,
  input  [1:0] In,
  output Z
);

  wire clock_1_out;
  wire [1:0] multiplexer_1_out, next_status_1_next_status, register_1_q;

  Clock clock_1 (.out(clock_1_out));
  next_status next_status_1 (.current_status(register_1_q), .In(In), .next_status(next_status_1_next_status));
  Multiplexer #(.width(2), .disabled(0), .enable("false")) multiplexer_1 (
    .in0(next_status_1_next_status), .in1(2'b00), .out(multiplexer_1_out), .sel(CLR));
  Register #(.width(2)) register_1 (.D(multiplexer_1_out), .Q(register_1_q), .clk(clock_1_out));  // open: en, clr
  ismatch ismatch_1 (.In(In), .status(register_1_q), .Z(Z));
endmodule

module next_status (
  input  [1:0] current_status,
  input  [1:0] In,
  output [1:0] next_status
);

  wire and_1_out, and_2_out, and_3_out, and_4_out, and_5_out, and_6_out, and_7_out, and_8_out, and_9_out,
       and_10_out, and_11_out, and_12_out, and_13_out, and_14_out, and_15_out, and_16_out, and_17_out,
       and_18_out, not_1_out, not_2_out, not_3_out, not_4_out, not_5_out, not_6_out, not_7_out, not_8_out,
       not_9_out, not_10_out, not_11_out, not_12_out, not_13_out, not_14_out, not_15_out, not_16_out,
       or_1_out, or_2_out, or_3_out, or_4_out;

  not not_1 (not_1_out, current_status[1]);
  not not_2 (not_2_out, current_status[1]);
  not not_3 (not_3_out, current_status[0]);
  not not_4 (not_4_out, current_status[0]);
  not not_5 (not_5_out, current_status[1]);
  not not_6 (not_6_out, current_status[0]);
  not not_7 (not_7_out, In[1]);
  not not_8 (not_8_out, current_status[1]);
  not not_9 (not_9_out, current_status[0]);
  not not_10 (not_10_out, In[1]);
  and and_1 (and_1_out, not_1_out, current_status[0]);
  not not_11 (not_11_out, In[1]);
  and and_2 (and_2_out, not_2_out, current_status[0]);
  not not_12 (not_12_out, In[0]);
  and and_3 (and_3_out, current_status[1], not_3_out);
  not not_13 (not_13_out, In[1]);
  and and_4 (and_4_out, current_status[1], not_4_out);
  not not_14 (not_14_out, In[0]);
  and and_5 (and_5_out, not_5_out, not_6_out);
  and and_6 (and_6_out, not_7_out, In[0]);
  and and_7 (and_7_out, not_8_out, current_status[0]);
  not not_15 (not_15_out, In[0]);
  and and_8 (and_8_out, current_status[1], not_9_out);
  not not_16 (not_16_out, In[0]);
  and and_9 (and_9_out, current_status[1], current_status[0]);
  and and_10 (and_10_out, not_10_out, In[0]);
  and and_11 (and_11_out, and_1_out, not_11_out);
  and and_12 (and_12_out, and_2_out, not_12_out);
  and and_13 (and_13_out, and_3_out, not_13_out);
  and and_14 (and_14_out, and_4_out, not_14_out);
  and and_15 (and_15_out, and_5_out, and_6_out);
  and and_16 (and_16_out, and_7_out, not_15_out);
  and and_17 (and_17_out, and_8_out, not_16_out);
  and and_18 (and_18_out, and_9_out, and_10_out);
  or or_1 (or_1_out, and_11_out, and_12_out);
  or or_2 (or_2_out, and_13_out, and_14_out);
  or or_3 (or_3_out, and_15_out, and_16_out);
  or or_4 (or_4_out, and_17_out, and_18_out);
  or or_5 (next_status[1], or_1_out, or_2_out);
  or or_6 (next_status[0], or_3_out, or_4_out);
endmodule

module ismatch (
  input  [1:0] In,
  input  [1:0] status,
  output Z
);

  wire comparator_1_eq, comparator_2_eq, comparator_3_eq, or_1_out;

  Comparator #(.width(2)) comparator_1 (.a(In), .b(2'b00), .eq(comparator_1_eq));  // open: gt, lt
  Comparator #(.width(2)) comparator_2 (.a(In), .b(2'b10), .eq(comparator_2_eq));  // open: gt, lt
  Comparator #(.width(2)) comparator_3 (.a(status), .b(2'b11), .eq(comparator_3_eq));  // open: gt, lt
  or or_1 (or_1_out, comparator_1_eq, comparator_2_eq);
  and and_1 (Z, or_1_out, comparator_3_eq);
endmodule

module temp (
  input  cur1,
  input  cur0,
  input  in1,
  input  in0,
  output next1,
  output next0
);

  wire and_1_out, and_2_out, and_3_out, and_4_out, and_5_out, and_6_out, and_7_out, and_8_out, and_9_out,
       and_10_out, and_11_out, and_12_out, and_13_out, and_14_out, and_15_out, and_16_out, and_17_out,
       and_18_out, not_1_out, not_2_out, not_3_out, not_4_out, not_5_out, not_6_out, not_7_out, not_8_out,
       not_9_out, not_10_out, not_11_out, not_12_out, not_13_out, not_14_out, not_15_out, not_16_out,
       or_1_out, or_2_out, or_3_out, or_4_out;

  not not_1 (not_1_out, cur1);
  and and_1 (and_1_out, not_1_out, cur0);
  not not_2 (not_2_out, in1);
  not not_3 (not_3_out, cur1);
  and and_2 (and_2_out, not_3_out, cur0);
  not not_4 (not_4_out, in0);
  and and_3 (and_3_out, cur1, not_5_out);
  not not_5 (not_5_out, cur0);
  not not_6 (not_6_out, in1);
  and and_4 (and_4_out, cur1, not_7_out);
  not not_7 (not_7_out, cur0);
  not not_8 (not_8_out, in0);
  not not_9 (not_9_out, cur1);
  and and_5 (and_5_out, not_9_out, not_10_out);
  not not_10 (not_10_out, cur0);
  not not_11 (not_11_out, in1);
  and and_6 (and_6_out, not_11_out, in0);
  not not_12 (not_12_out, cur1);
  and and_7 (and_7_out, not_12_out, cur0);
  not not_13 (not_13_out, in0);
  and and_8 (and_8_out, cur1, not_14_out);
  not not_14 (not_14_out, cur0);
  not not_15 (not_15_out, in0);
  and and_9 (and_9_out, cur1, cur0);
  not not_16 (not_16_out, in1);
  and and_10 (and_10_out, not_16_out, in0);
  and and_11 (and_11_out, and_1_out, not_2_out);
  and and_12 (and_12_out, and_2_out, not_4_out);
  and and_13 (and_13_out, and_3_out, not_6_out);
  and and_14 (and_14_out, and_4_out, not_8_out);
  and and_15 (and_15_out, and_5_out, and_6_out);
  and and_16 (and_16_out, and_7_out, not_13_out);
  and and_17 (and_17_out, and_8_out, not_15_out);
  and and_18 (and_18_out, and_9_out, and_10_out);
  or or_1 (or_1_out, and_11_out, and_12_out);
  or or_2 (or_2_out, and_13_out, and_14_out);
  or or_3 (or_3_out, and_15_out, and_16_out);
  or or_4 (or_4_out, and_17_out, and_18_out);
  or or_5 (next1, or_1_out, or_2_out);
  or or_6 (next0, or_3_out, or_4_out);
endmodule
