// Logisim project ftoi.circ as structural Verilog: 2 circuits, main circuit ftoi
module ftoi (
  input  [15:0] in_1,
  output [31:0] out_2
);

  wire comparator_1_eq;
  wire [31:0] floor_func_1_out_4;

  floor_func floor_func_1 (.S(in_1[15]), .E(in_1[14:10]), .M(in_1[9:0]), .out_4(floor_func_1_out_4));
  Comparator #(.width(5), .mode("unsigned")) comparator_1 (
    .a(in_1[14:10]), .b({5{1'b1}}), .eq(comparator_1_eq));  // open: gt, lt
  Multiplexer #(.width(32), .disabled(0), .enable("false")) multiplexer_1 (
    .in0(floor_func_1_out_4), .in1({32{1'b0}}), .out(out_2), .sel(comparator_1_eq));
endmodule

module floor_func (
  input  S,
  input  [4:0] E,
  input  [9:0] M,
  output [31:0] out_4
);

  wire comparator_1_eq, comparator_2_lt;
  wire [4:0] negator_1_out, subtractor_1_out;
  wire [31:0] adder_1_out, bit_extender_1_out, multiplexer_1_out, multiplexer_2_out, negator_2_out,
       shifter_1_out, shifter_2_out, shifter_3_out;

  assign bit_extender_1_out = {{22{1'b0}}, M};  // Bit_Extender bit_extender_1
  Subtractor #(.width(5)) subtractor_1 (.a(E), .b(5'b01111), .out(subtractor_1_out));  // open: bin, bout
  Comparator #(.width(5)) comparator_1 (.a(E), .b({5{1'b0}}), .eq(comparator_1_eq));  // open: gt, lt
  Adder #(.width(32)) adder_1 (.a(bit_extender_1_out), .b(32'h400), .out(adder_1_out));  // open: cin, cout
  Multiplexer #(.width(32), .disabled(0), .enable("false")) multiplexer_1 (
    .in0(adder_1_out), .in1(bit_extender_1_out), .out(multiplexer_1_out), .sel(comparator_1_eq));
  Negator #(.width(5)) negator_1 (.in(subtractor_1_out), .out(negator_1_out));
  Shifter #(.width(32), .shift("lr")) shifter_1 (.in(multiplexer_1_out), .\dist (negator_1_out), .out(shifter_1_out));
  Comparator #(.width(5)) comparator_2 (.a(subtractor_1_out), .b({5{1'b0}}), .lt(comparator_2_lt));  // open: gt, eq
  Shifter #(.width(32)) shifter_2 (.in(multiplexer_1_out), .\dist (subtractor_1_out), .out(shifter_2_out));
  Multiplexer #(.width(32), .disabled(0), .enable("false")) multiplexer_2 (
    .in0(shifter_2_out), .in1(shifter_1_out), .out(multiplexer_2_out), .sel(comparator_2_lt));
  Shifter #(.width(32), .shift("lr")) shifter_3 (.in(multiplexer_2_out), .\dist (5'b01010), .out(shifter_3_out));
  // Probe on out_4
  Negator #(.width(32)) negator_2 (.in(shifter_3_out), .out(negator_2_out));
  Multiplexer #(.width(32), .disabled(0), .enable("false")) multiplexer_3 (
    .in0(shifter_3_out), .in1(negator_2_out), .out(out_4), .sel(S));
endmodule
