// Logisim project navigation.circ as structural Verilog: 3 circuits, main circuit navigation
module navigation (
  input  [1:0] dir,
  input  clk,
  input  reset,
  output arrive,
  output hit
);

  wire next_status_1_hit;
  wire [2:0] next_status_1_out_3, register_1_q;

  next_status next_status_1 (
    .current_state(register_1_q), .dir(dir), .out_3(next_status_1_out_3), .hit(next_status_1_hit));
  Register #(.width(3)) register_1 (.D(next_status_1_out_3), .Q(register_1_q), .clk(clk), .clr(reset));  // open: en
  Register #(.width(1)) register_2 (.D(next_status_1_hit), .Q(hit), .clk(clk), .clr(reset));  // open: en
  Comparator #(.width(3)) comparator_1 (.a(3'b100), .b(register_1_q), .eq(arrive));  // open: gt, lt
endmodule

module next_status (
  input  [2:0] current_state,
  input  [1:0] dir,
  output [2:0] out_3,
  output hit
);

  wire and_1_out, and_2_out, and_3_out, and_4_out, and_5_out, and_6_out, and_7_out, and_8_out, and_9_out,
       and_10_out, and_11_out, and_12_out, and_13_out, and_14_out, and_15_out, and_16_out, and_17_out,
       and_18_out, and_19_out, and_20_out, and_21_out, and_22_out, and_23_out, and_24_out, and_25_out,
       and_26_out, and_27_out, and_28_out, and_29_out, and_30_out, and_31_out, and_32_out, and_33_out,
       and_34_out, and_35_out, and_36_out, and_37_out, and_38_out, and_39_out, and_40_out, and_41_out,
       and_42_out, and_43_out, and_44_out, and_45_out, and_46_out, and_47_out, and_48_out, and_49_out,
       and_50_out, and_51_out, and_52_out, and_53_out, and_54_out, not_1_out, not_2_out, not_3_out,
       not_4_out, not_5_out, not_6_out, not_7_out, not_8_out, not_9_out, not_10_out, not_11_out, not_12_out,
       not_13_out, not_14_out, not_15_out, not_16_out, not_17_out, not_18_out, not_19_out, not_20_out,
       not_21_out, not_22_out, not_23_out, not_24_out, not_25_out, not_26_out, not_27_out, not_28_out,
       not_29_out, not_30_out, not_31_out, not_32_out, or_1_out, or_2_out, or_3_out, or_4_out, or_5_out,
       or_6_out, or_7_out, or_8_out, or_9_out, or_10_out, or_12_out, or_13_out, or_15_out, or_16_out;

  and and_1 (and_1_out, current_state[1], not_1_out);
  not not_1 (not_1_out, current_state[0]);
  not not_2 (not_2_out, dir[1]);
  and and_2 (and_2_out, not_2_out, not_3_out);
  not not_3 (not_3_out, dir[0]);
  and and_3 (and_3_out, current_state[1], current_state[0]);
  not not_4 (not_4_out, dir[1]);
  and and_4 (and_4_out, not_4_out, dir[0]);
  and and_5 (and_5_out, current_state[2], current_state[0]);
  not not_5 (not_5_out, dir[1]);
  and and_6 (and_6_out, current_state[2], current_state[1]);
  not not_6 (not_6_out, dir[1]);
  not not_7 (not_7_out, current_state[1]);
  and and_7 (and_7_out, not_7_out, current_state[0]);
  not not_8 (not_8_out, dir[1]);
  and and_8 (and_8_out, current_state[0], not_9_out);
  not not_9 (not_9_out, dir[1]);
  not not_10 (not_10_out, dir[0]);
  and and_9 (and_9_out, current_state[1], not_11_out);
  not not_11 (not_11_out, current_state[0]);
  not not_12 (not_12_out, dir[1]);
  and and_10 (and_10_out, not_12_out, dir[0]);
  and and_11 (and_11_out, current_state[1], not_13_out);
  not not_13 (not_13_out, current_state[0]);
  and and_12 (and_12_out, dir[1], not_14_out);
  not not_14 (not_14_out, dir[0]);
  and and_13 (and_13_out, current_state[1], current_state[0]);
  and and_14 (and_14_out, dir[1], dir[0]);
  and and_15 (and_15_out, current_state[2], current_state[0]);
  not not_15 (not_15_out, current_state[2]);
  and and_16 (and_16_out, not_15_out, not_16_out);
  not not_16 (not_16_out, current_state[1]);
  not not_17 (not_17_out, dir[1]);
  and and_17 (and_17_out, not_17_out, not_18_out);
  not not_18 (not_18_out, dir[0]);
  and and_18 (and_18_out, current_state[0], dir[1]);
  and and_19 (and_19_out, current_state[1], dir[1]);
  and and_20 (and_20_out, current_state[1], current_state[0]);
  not not_19 (not_19_out, dir[0]);
  not not_20 (not_20_out, current_state[2]);
  and and_21 (and_21_out, not_20_out, not_21_out);
  not not_21 (not_21_out, current_state[1]);
  not not_22 (not_22_out, current_state[0]);
  and and_22 (and_22_out, not_22_out, dir[0]);
  not not_23 (not_23_out, current_state[2]);
  and and_23 (and_23_out, not_23_out, not_24_out);
  not not_24 (not_24_out, current_state[0]);
  not not_25 (not_25_out, dir[1]);
  and and_24 (and_24_out, not_25_out, dir[0]);
  not not_26 (not_26_out, current_state[2]);
  and and_25 (and_25_out, not_26_out, not_27_out);
  not not_27 (not_27_out, current_state[0]);
  and and_26 (and_26_out, dir[1], not_28_out);
  not not_28 (not_28_out, dir[0]);
  and and_27 (and_27_out, current_state[0], dir[1]);
  and and_28 (and_28_out, current_state[1], current_state[0]);
  not not_29 (not_29_out, dir[1]);
  and and_29 (and_29_out, not_29_out, not_30_out);
  not not_30 (not_30_out, dir[0]);
  and and_30 (and_30_out, current_state[2], current_state[0]);
  not not_31 (not_31_out, dir[1]);
  and and_31 (and_31_out, and_1_out, and_2_out);
  and and_32 (and_32_out, and_3_out, and_4_out);
  and and_33 (and_33_out, and_5_out, not_5_out);
  and and_34 (and_34_out, and_6_out, not_6_out);
  and and_35 (and_35_out, and_7_out, not_8_out);
  and and_36 (and_36_out, and_8_out, not_10_out);
  and and_37 (and_37_out, and_9_out, and_10_out);
  and and_38 (and_38_out, and_11_out, and_12_out);
  and and_39 (and_39_out, and_13_out, and_14_out);
  and and_40 (and_40_out, and_15_out, dir[1]);
  and and_41 (and_41_out, current_state[2], current_state[1]);
  and and_42 (and_42_out, and_16_out, and_17_out);
  and and_43 (and_43_out, and_18_out, dir[0]);
  and and_44 (and_44_out, and_19_out, dir[0]);
  and and_45 (and_45_out, and_20_out, not_19_out);
  and and_46 (and_46_out, and_21_out, and_22_out);
  and and_47 (and_47_out, and_23_out, and_24_out);
  and and_48 (and_48_out, and_25_out, and_26_out);
  and and_49 (and_49_out, and_27_out, dir[0]);
  and and_50 (and_50_out, and_28_out, and_29_out);
  and and_51 (and_51_out, and_30_out, not_31_out);
  and and_52 (and_52_out, current_state[2], current_state[1]);
  not not_32 (not_32_out, dir[1]);
  or or_1 (or_1_out, and_31_out, and_32_out);
  or or_2 (or_2_out, and_33_out, and_34_out);
  or or_3 (or_3_out, and_35_out, and_36_out);
  or or_4 (or_4_out, and_37_out, and_38_out);
  or or_5 (or_5_out, and_39_out, and_40_out);
  and and_53 (and_53_out, and_41_out, dir[1]);
  or or_6 (or_6_out, and_42_out, and_43_out);
  or or_7 (or_7_out, and_44_out, and_45_out);
  or or_8 (or_8_out, and_46_out, and_47_out);
  or or_9 (or_9_out, and_48_out, and_49_out);
  or or_10 (or_10_out, and_50_out, and_51_out);
  and and_54 (and_54_out, and_52_out, not_32_out);
  or or_11 (out_3[2], or_1_out, or_2_out);
  or or_12 (or_12_out, or_3_out, or_4_out);
  or or_13 (or_13_out, or_5_out, and_53_out);
  or or_14 (out_3[0], or_6_out, or_7_out);
  or or_15 (or_15_out, or_8_out, or_9_out);
  or or_16 (or_16_out, or_10_out, and_54_out);
  or or_17 (out_3[1], or_12_out, or_13_out);
  or or_18 (hit, or_15_out, or_16_out);
endmodule

module \input  (
  input  cs2,
  input  cs1,
  input  cs0,
  input  dir1,
  input  dir0,
  output ns2,
  output ns1,
  output ns0,
  output hit
);

  wire and_1_out, and_2_out, and_3_out, and_4_out, and_5_out, and_6_out, and_7_out, and_8_out, and_9_out,
       and_10_out, and_11_out, and_12_out, and_13_out, and_14_out, and_15_out, and_16_out, and_17_out,
       and_18_out, and_19_out, and_20_out, and_21_out, and_22_out, and_23_out, and_24_out, and_25_out,
       and_26_out, and_27_out, and_28_out, and_29_out, and_30_out, and_31_out, and_32_out, and_33_out,
       and_34_out, and_35_out, and_36_out, and_37_out, and_38_out, and_39_out, and_40_out, and_41_out,
       and_42_out, and_43_out, and_44_out, and_45_out, and_46_out, and_47_out, and_48_out, and_49_out,
       and_50_out, and_51_out, and_52_out, and_53_out, and_54_out, not_1_out, not_2_out, not_3_out,
       not_4_out, not_5_out, not_6_out, not_7_out, not_8_out, not_9_out, not_10_out, not_11_out, not_12_out,
       not_13_out, not_14_out, not_15_out, not_16_out, not_17_out, not_18_out, not_19_out, not_20_out,
       not_21_out, not_22_out, not_23_out, not_24_out, not_25_out, not_26_out, not_27_out, not_28_out,
       not_29_out, not_30_out, not_31_out, not_32_out, or_1_out, or_2_out, or_3_out, or_4_out, or_5_out,
       or_6_out, or_7_out, or_8_out, or_9_out, or_10_out, or_12_out, or_13_out, or_15_out, or_16_out;

  not not_1 (not_1_out, cs0);
  not not_2 (not_2_out, dir1);
  not not_3 (not_3_out, dir0);
  not not_4 (not_4_out, dir1);
  not not_5 (not_5_out, cs1);
  not not_6 (not_6_out, dir1);
  not not_7 (not_7_out, cs0);
  not not_8 (not_8_out, dir1);
  not not_9 (not_9_out, cs0);
  not not_10 (not_10_out, dir0);
  not not_11 (not_11_out, cs2);
  not not_12 (not_12_out, cs1);
  not not_13 (not_13_out, dir1);
  not not_14 (not_14_out, dir0);
  not not_15 (not_15_out, cs2);
  not not_16 (not_16_out, cs1);
  not not_17 (not_17_out, cs0);
  not not_18 (not_18_out, cs2);
  not not_19 (not_19_out, cs0);
  not not_20 (not_20_out, dir1);
  not not_21 (not_21_out, cs2);
  not not_22 (not_22_out, cs0);
  not not_23 (not_23_out, dir0);
  not not_24 (not_24_out, dir1);
  not not_25 (not_25_out, dir0);
  and and_1 (and_1_out, cs1, not_1_out);
  and and_2 (and_2_out, not_2_out, not_3_out);
  and and_3 (and_3_out, cs1, cs0);
  and and_4 (and_4_out, not_4_out, dir0);
  and and_5 (and_5_out, cs2, cs0);
  not not_26 (not_26_out, dir1);
  and and_6 (and_6_out, cs2, cs1);
  not not_27 (not_27_out, dir1);
  and and_7 (and_7_out, not_5_out, cs0);
  not not_28 (not_28_out, dir1);
  and and_8 (and_8_out, cs0, not_6_out);
  not not_29 (not_29_out, dir0);
  and and_9 (and_9_out, cs1, not_7_out);
  and and_10 (and_10_out, not_8_out, dir0);
  and and_11 (and_11_out, cs1, not_9_out);
  and and_12 (and_12_out, dir1, not_10_out);
  and and_13 (and_13_out, cs1, cs0);
  and and_14 (and_14_out, dir1, dir0);
  and and_15 (and_15_out, cs2, cs0);
  and and_16 (and_16_out, not_11_out, not_12_out);
  and and_17 (and_17_out, not_13_out, not_14_out);
  and and_18 (and_18_out, cs0, dir1);
  and and_19 (and_19_out, cs1, dir1);
  and and_20 (and_20_out, cs1, cs0);
  not not_30 (not_30_out, dir0);
  and and_21 (and_21_out, not_15_out, not_16_out);
  and and_22 (and_22_out, not_17_out, dir0);
  and and_23 (and_23_out, not_18_out, not_19_out);
  and and_24 (and_24_out, not_20_out, dir0);
  and and_25 (and_25_out, not_21_out, not_22_out);
  and and_26 (and_26_out, dir1, not_23_out);
  and and_27 (and_27_out, cs0, dir1);
  and and_28 (and_28_out, cs1, cs0);
  and and_29 (and_29_out, not_24_out, not_25_out);
  and and_30 (and_30_out, cs2, cs0);
  not not_31 (not_31_out, dir1);
  and and_31 (and_31_out, and_1_out, and_2_out);
  or or_1 (or_1_out, and_31_out, and_32_out);
  and and_32 (and_32_out, and_3_out, and_4_out);
  and and_33 (and_33_out, and_5_out, not_26_out);
  or or_2 (or_2_out, and_33_out, and_34_out);
  and and_34 (and_34_out, and_6_out, not_27_out);
  and and_35 (and_35_out, and_7_out, not_28_out);
  or or_3 (or_3_out, and_35_out, and_36_out);
  and and_36 (and_36_out, and_8_out, not_29_out);
  and and_37 (and_37_out, and_9_out, and_10_out);
  or or_4 (or_4_out, and_37_out, and_38_out);
  and and_38 (and_38_out, and_11_out, and_12_out);
  and and_39 (and_39_out, and_13_out, and_14_out);
  or or_5 (or_5_out, and_39_out, and_40_out);
  and and_40 (and_40_out, and_15_out, dir1);
  and and_41 (and_41_out, cs2, cs1);
  and and_42 (and_42_out, and_41_out, dir1);
  and and_43 (and_43_out, and_16_out, and_17_out);
  or or_6 (or_6_out, and_43_out, and_44_out);
  and and_44 (and_44_out, and_18_out, dir0);
  and and_45 (and_45_out, and_19_out, dir0);
  or or_7 (or_7_out, and_45_out, and_46_out);
  and and_46 (and_46_out, and_20_out, not_30_out);
  and and_47 (and_47_out, and_21_out, and_22_out);
  or or_8 (or_8_out, and_47_out, and_48_out);
  and and_48 (and_48_out, and_23_out, and_24_out);
  and and_49 (and_49_out, and_25_out, and_26_out);
  or or_9 (or_9_out, and_49_out, and_50_out);
  and and_50 (and_50_out, and_27_out, dir0);
  and and_51 (and_51_out, and_28_out, and_29_out);
  or or_10 (or_10_out, and_51_out, and_52_out);
  and and_52 (and_52_out, and_30_out, not_31_out);
  and and_53 (and_53_out, cs2, cs1);
  and and_54 (and_54_out, and_53_out, not_32_out);
  not not_32 (not_32_out, dir1);
  or or_11 (ns2, or_1_out, or_2_out);
  or or_12 (or_12_out, or_3_out, or_4_out);
  or or_13 (or_13_out, or_5_out, and_42_out);
  or or_14 (ns0, or_6_out, or_7_out);
  or or_15 (or_15_out, or_8_out, or_9_out);
  or or_16 (or_16_out, or_10_out, and_54_out);
  or or_17 (ns1, or_12_out, or_13_out);
  or or_18 (hit, or_15_out, or_16_out);
endmodule
