// Logisim project Single_Cycle_CPU.circ as structural Verilog: 8 circuits, main circuit main
module main (
  input  Reset,
  output [31:0] Instr,
  output RegWrite,
  output [4:0] RegAddr,
  output [31:0] RegData,
  output MemWrite,
  output [4:0] MemAddr,
  output [31:0] MemData
);

  wire alu_1_equal, clock_1_out, controller_1_dmre, controller_1_mux1, controller_1_mux2, controller_1_mux3,
       controller_1_npcop;
  wire [1:0] controller_1_aluop, controller_1_extop;
  wire [31:0] alu_1_result, dm_1_rd, ext_1_extimm, grf_1_rd1, multiplexer_2_out;

  Clock clock_1 (.out(clock_1_out));
  IFU ifu_1 (.Reset(Reset), .CLK(clock_1_out), .Instr(Instr), .NPCOp(controller_1_npcop), .flip(alu_1_equal));
  EXT ext_1 (.imm(Instr[15:0]), .EXTOp(controller_1_extop), .EXTimm(ext_1_extimm));
  Multiplexer #(.width(5), .disabled(0), .enable("false")) multiplexer_1 (
    .in0(Instr[20:16]), .in1(Instr[15:11]), .out(RegAddr), .sel(controller_1_mux1));
  GRF grf_1 (
    .WD(RegData), .WA(RegAddr), .RA1(Instr[25:21]), .RA2(Instr[20:16]), .RD1(grf_1_rd1), .RD2(MemData),
    .CLK(clock_1_out), .Reset(Reset), .WE(RegWrite));
  ALU alu_1 (
    .num1(grf_1_rd1), .num2(multiplexer_2_out), .result({alu_1_result[31:7], MemAddr, alu_1_result[1:0]}),
    .equal(alu_1_equal), .ALUOp(controller_1_aluop));
  Multiplexer #(.width(32), .disabled(0), .enable("false")) multiplexer_2 (
    .in0(MemData), .in1(ext_1_extimm), .out(multiplexer_2_out), .sel(controller_1_mux2));
  Multiplexer #(.width(32), .disabled(0), .enable("false")) multiplexer_3 (
    .in0({alu_1_result[31:7], MemAddr, alu_1_result[1:0]}), .in1(dm_1_rd), .out(RegData),
    .sel(controller_1_mux3));
  Controller controller_1 (
    .opcode(Instr[31:26]), .funct(Instr[5:0]), .MUX1(controller_1_mux1), .MUX2(controller_1_mux2),
    .MUX3(controller_1_mux3), .NPCOp(controller_1_npcop), .GRFWE(RegWrite), .DMWE(MemWrite),
    .ALUOp(controller_1_aluop), .EXTOp(controller_1_extop), .DMRE(controller_1_dmre));
  DM dm_1 (
    .Reset(Reset), .CLK(clock_1_out), .Addr(MemAddr), .WD(MemData), .RD(dm_1_rd), .WE(MemWrite),
    .RE(controller_1_dmre));

  // Other names for the same wires on the sheet: RedAddr[4:0] = RegAddr
endmodule

module IFU (
  input  Reset,
  input  CLK,
  input  flip,
  input  NPCOp,
  output [31:0] Instr
);

  wire [31:0] npc_1_npc, PC_q;

  Register #(.width(32)) PC (.D(npc_1_npc), .Q(PC_q), .clk(CLK), .clr(Reset));  // open: en
  NPC npc_1 (.PC(PC_q), .offset(Instr[15:0]), .flip(flip), .NPCOp(NPCOp), .NPC(npc_1_npc));
  ROM #(.addrWidth(5), .dataWidth(32)) rom_1 (.addr(PC_q[6:2]), .data(Instr));  // open: sel
endmodule

module GRF (
  input  CLK,
  input  Reset,
  input  WE,
  input  [4:0] RA1,
  input  [4:0] RA2,
  input  [4:0] WA,
  input  [31:0] WD,
  output [31:0] RD1,
  output [31:0] RD2
);

  wire e1, e2, e3, e4, e5, e6, e7, e8, e9, e10, e11, e12, e13, e14, e15, e16, e17, e18, e19, e20, e21, e22,
       e23, e24, e25, e26, e27, e28, e29, e30, e31;
  wire [31:0] r0, r1, r2, r3, r4, r5, r6, r7, r8, r9, r10, r11, r12, r13, r14, r15, r16, r17, r18, r19, r20,
       r21, r22, r23, r24, r25, r26, r27, r28, r29, r30, r31, w1, w2, w3, w4, w5, w6, w7, w8, w9, w10, w11,
       w12, w13, w14, w15, w16, w17, w18, w19, w20, w21, w22, w23, w24, w25, w26, w27, w28, w29, w30, w31;

  Register #(.width(32)) register_1 (.Q(r0), .clk(CLK), .clr(Reset));  // open: D, en
  Register #(.width(32)) register_2 (.D(w1), .en(e1), .Q(r1), .clk(CLK), .clr(Reset));
  Register #(.width(32)) register_3 (.D(w2), .en(e2), .Q(r2), .clk(CLK), .clr(Reset));
  Register #(.width(32)) register_4 (.D(w3), .en(e3), .Q(r3), .clk(CLK), .clr(Reset));
  Register #(.width(32)) register_5 (.D(w4), .en(e4), .Q(r4), .clk(CLK), .clr(Reset));
  Register #(.width(32)) register_6 (.D(w5), .en(e5), .Q(r5), .clk(CLK), .clr(Reset));
  Register #(.width(32)) register_7 (.D(w6), .en(e6), .Q(r6), .clk(CLK), .clr(Reset));
  Register #(.width(32)) register_8 (.D(w7), .en(e7), .Q(r7), .clk(CLK), .clr(Reset));
  Register #(.width(32)) register_9 (.D(w8), .en(e8), .Q(r8), .clk(CLK), .clr(Reset));
  Register #(.width(32)) register_10 (.D(w9), .en(e9), .Q(r9), .clk(CLK), .clr(Reset));
  Register #(.width(32)) register_11 (.D(w10), .en(e10), .Q(r10), .clk(CLK), .clr(Reset));
  Register #(.width(32)) register_12 (.D(w11), .en(e11), .Q(r11), .clk(CLK), .clr(Reset));
  Register #(.width(32)) register_13 (.D(w12), .en(e12), .Q(r12), .clk(CLK), .clr(Reset));
  Register #(.width(32)) register_14 (.D(w13), .en(e13), .Q(r13), .clk(CLK), .clr(Reset));
  Register #(.width(32)) register_15 (.D(w14), .en(e14), .Q(r14), .clk(CLK), .clr(Reset));
  Register #(.width(32)) register_16 (.D(w15), .en(e15), .Q(r15), .clk(CLK), .clr(Reset));
  Register #(.width(32)) register_17 (.D(w16), .en(e16), .Q(r16), .clk(CLK), .clr(Reset));
  Register #(.width(32)) register_18 (.D(w17), .en(e17), .Q(r17), .clk(CLK), .clr(Reset));
  Register #(.width(32)) register_19 (.D(w18), .en(e18), .Q(r18), .clk(CLK), .clr(Reset));
  Register #(.width(32)) register_20 (.D(w19), .en(e19), .Q(r19), .clk(CLK), .clr(Reset));
  Register #(.width(32)) register_21 (.D(w20), .en(e20), .Q(r20), .clk(CLK), .clr(Reset));
  Register #(.width(32)) register_22 (.D(w21), .en(e21), .Q(r21), .clk(CLK), .clr(Reset));
  Register #(.width(32)) register_23 (.D(w22), .en(e22), .Q(r22), .clk(CLK), .clr(Reset));
  Register #(.width(32)) register_24 (.D(w23), .en(e23), .Q(r23), .clk(CLK), .clr(Reset));
  Register #(.width(32)) register_25 (.D(w24), .en(e24), .Q(r24), .clk(CLK), .clr(Reset));
  Register #(.width(32)) register_26 (.D(w25), .en(e25), .Q(r25), .clk(CLK), .clr(Reset));
  Register #(.width(32)) register_27 (.D(w26), .en(e26), .Q(r26), .clk(CLK), .clr(Reset));
  Register #(.width(32)) register_28 (.D(w27), .en(e27), .Q(r27), .clk(CLK), .clr(Reset));
  Register #(.width(32)) register_29 (.D(w28), .en(e28), .Q(r28), .clk(CLK), .clr(Reset));
  Register #(.width(32)) register_30 (.D(w29), .en(e29), .Q(r29), .clk(CLK), .clr(Reset));
  Register #(.width(32)) register_31 (.D(w30), .en(e30), .Q(r30), .clk(CLK), .clr(Reset));
  Register #(.width(32)) register_32 (.D(w31), .en(e31), .Q(r31), .clk(CLK), .clr(Reset));
  Demultiplexer #(.select(5), .width(32), .disabled(0), .enable("false")) demultiplexer_1 (
    .out1(w1), .out2(w2), .out3(w3), .out4(w4), .out5(w5), .out6(w6), .out7(w7), .out8(w8), .out9(w9),
    .out10(w10), .out11(w11), .out12(w12), .out13(w13), .out14(w14), .out15(w15), .out16(w16), .out17(w17),
    .out18(w18), .out19(w19), .out20(w20), .out21(w21), .out22(w22), .out23(w23), .out24(w24), .out25(w25),
    .out26(w26), .out27(w27), .out28(w28), .out29(w29), .out30(w30), .out31(w31), .in(WD), .sel(WA));  // open: out0
  Multiplexer #(.select(5), .width(32), .disabled(0), .enable("false")) multiplexer_1 (
    .in0(r0), .in1(r1), .in2(r2), .in3(r3), .in4(r4), .in5(r5), .in6(r6), .in7(r7), .in8(r8), .in9(r9),
    .in10(r10), .in11(r11), .in12(r12), .in13(r13), .in14(r14), .in15(r15), .in16(r16), .in17(r17),
    .in18(r18), .in19(r19), .in20(r20), .in21(r21), .in22(r22), .in23(r23), .in24(r24), .in25(r25),
    .in26(r26), .in27(r27), .in28(r28), .in29(r29), .in30(r30), .in31(r31), .out(RD1), .sel(RA1));
  Demultiplexer #(.select(5), .disabled(0), .enable("false")) demultiplexer_2 (
    .out1(e1), .out2(e2), .out3(e3), .out4(e4), .out5(e5), .out6(e6), .out7(e7), .out8(e8), .out9(e9),
    .out10(e10), .out11(e11), .out12(e12), .out13(e13), .out14(e14), .out15(e15), .out16(e16), .out17(e17),
    .out18(e18), .out19(e19), .out20(e20), .out21(e21), .out22(e22), .out23(e23), .out24(e24), .out25(e25),
    .out26(e26), .out27(e27), .out28(e28), .out29(e29), .out30(e30), .out31(e31), .in(WE), .sel(WA));  // open: out0
  Multiplexer #(.select(5), .width(32), .disabled(0), .enable("false")) multiplexer_2 (
    .in0(r0), .in1(r1), .in2(r2), .in3(r3), .in4(r4), .in5(r5), .in6(r6), .in7(r7), .in8(r8), .in9(r9),
    .in10(r10), .in11(r11), .in12(r12), .in13(r13), .in14(r14), .in15(r15), .in16(r16), .in17(r17),
    .in18(r18), .in19(r19), .in20(r20), .in21(r21), .in22(r22), .in23(r23), .in24(r24), .in25(r25),
    .in26(r26), .in27(r27), .in28(r28), .in29(r29), .in30(r30), .in31(r31), .out(RD2), .sel(RA2));
endmodule

module ALU (
  input  [31:0] num1,
  input  [31:0] num2,
  input  [1:0] ALUOp,
  output [31:0] result,
  output equal
);

  wire [31:0] adder_1_out, or_1_out, subtractor_1_out;

  Adder #(.width(32)) adder_1 (.a(num1), .b(num2), .out(adder_1_out));  // open: cin, cout
  Subtractor #(.width(32)) subtractor_1 (.a(num1), .b(num2), .out(subtractor_1_out));  // open: bin, bout
  assign or_1_out = num1 | num2;  // OR_Gate or_1, 32 bits wide
  Comparator #(.width(32)) comparator_1 (.a(num1), .b(num2), .eq(equal));  // open: gt, lt
  Multiplexer #(.select(2), .width(32), .disabled(0), .enable("false")) multiplexer_1 (
    .in0(adder_1_out), .in1(subtractor_1_out), .in2(or_1_out), .out(result), .sel(ALUOp));  // open: in3
endmodule

module DM (
  input  Reset,
  input  CLK,
  input  [4:0] Addr,
  input  [31:0] WD,
  input  WE,
  input  RE,
  output [31:0] RD
);

  RAM #(.addrWidth(5), .dataWidth(32), .bus("separate")) ram_1 (
    .addr(Addr), .din(WD), .data(RD), .str(WE), .clk(CLK), .ld(RE), .clr(Reset));  // open: sel
endmodule

module EXT (
  input  [15:0] imm,
  input  [1:0] EXTOp,
  output [31:0] EXTimm
);

  wire [31:0] bit_extender_1_out, bit_extender_2_out;

  assign bit_extender_1_out = {{16{imm[15]}}, imm};  // Bit_Extender bit_extender_1
  assign bit_extender_2_out = {{16{1'b0}}, imm};  // Bit_Extender bit_extender_2
  Multiplexer #(.select(2), .width(32), .disabled(0), .enable("false")) multiplexer_1 (
    .in0(bit_extender_1_out), .in1(bit_extender_2_out), .in2({imm, {16{1'b0}}}), .out(EXTimm), .sel(EXTOp));  // open: in3
endmodule

module Controller (
  input  [5:0] opcode,
  input  [5:0] funct,
  output MUX1,
  output MUX2,
  output MUX3,
  output NPCOp,
  output GRFWE,
  output DMWE,
  output DMRE,
  output [1:0] ALUOp,
  output [1:0] EXTOp
);

  wire addu, and_1_out, nop, not_1_out, not_2_out, not_3_out, not_4_out, not_5_out, not_6_out, not_7_out,
       not_8_out, not_9_out, not_10_out, not_11_out, not_12_out, subu;

  not not_1 (not_1_out, opcode[4]);
  not not_2 (not_2_out, opcode[5]);
  not not_3 (not_3_out, opcode[2]);
  not not_4 (not_4_out, opcode[3]);
  or or_1 (MUX1, addu, subu);
  not not_5 (not_5_out, opcode[0]);
  not not_6 (not_6_out, opcode[1]);
  or or_2 (MUX2, EXTOp[0], DMRE, DMWE, EXTOp[1]);
  and and_1 (and_1_out, not_2_out, not_1_out, not_4_out, not_3_out, not_6_out, not_5_out);
  and and_2 (EXTOp[0], not_2_out, not_1_out, opcode[3], opcode[2], not_6_out, opcode[0]);
  and and_3 (DMRE, opcode[5], not_1_out, not_4_out, not_3_out, opcode[1], opcode[0]);
  and and_4 (DMWE, opcode[5], not_1_out, opcode[3], not_3_out, opcode[1], opcode[0]);
  and and_5 (NPCOp, not_2_out, not_1_out, not_4_out, opcode[2], not_6_out, not_5_out);
  and and_6 (EXTOp[1], not_2_out, not_1_out, opcode[3], opcode[2], opcode[1], opcode[0]);
  or or_3 (GRFWE, addu, subu, EXTOp[0], DMRE, EXTOp[1]);
  not not_7 (not_7_out, funct[5]);
  not not_8 (not_8_out, funct[4]);
  or or_4 (ALUOp[1], EXTOp[0], NPCOp, EXTOp[1]);
  not not_9 (not_9_out, funct[2]);
  not not_10 (not_10_out, funct[3]);
  or or_5 (ALUOp[0], subu, NPCOp);
  not not_11 (not_11_out, funct[0]);
  not not_12 (not_12_out, funct[1]);
  and and_7 (addu, funct[5], not_8_out, not_10_out, not_9_out, not_12_out, funct[0], and_1_out);
  and and_8 (subu, funct[5], not_8_out, not_10_out, not_9_out, funct[1], funct[0], and_1_out);
  and and_9 (nop, not_7_out, not_8_out, not_10_out, not_9_out, not_12_out, not_11_out, and_1_out);

  assign MUX3 = DMRE;

  // Other names for the same wires on the sheet: beq = NPCOp; ori = EXTOp[0]; lui = EXTOp[1]; lw = DMRE; sw = DMWE
endmodule

module NPC (
  input  [31:0] PC,
  input  [15:0] offset,
  input  flip,
  input  NPCOp,
  output [31:0] NPC
);

  wire [31:0] adder_1_out, adder_2_out, bit_extender_1_out, multiplexer_1_out, shifter_1_out;

  assign bit_extender_1_out = {{16{offset[15]}}, offset};  // Bit_Extender bit_extender_1
  Shifter #(.width(32)) shifter_1 (.in(bit_extender_1_out), .\dist (5'b00010), .out(shifter_1_out));
  Adder #(.width(32)) adder_1 (.a(PC), .b(32'h4), .out(adder_1_out));  // open: cin, cout
  Multiplexer #(.width(32), .enable("false")) multiplexer_1 (
    .in0({32{1'b0}}), .in1(shifter_1_out), .out(multiplexer_1_out), .sel(flip));
  Adder #(.width(32)) adder_2 (.a(adder_1_out), .b(multiplexer_1_out), .out(adder_2_out));  // open: cin, cout
  Multiplexer #(.width(32), .enable("false")) multiplexer_2 (
    .in0(adder_1_out), .in1(adder_2_out), .out(NPC), .sel(NPCOp));
endmodule
