// Logisim project 2^n mod 5.circ as structural Verilog: 2 circuits, main circuit mod5
module mod5 (
  input  in_1,
  output out_2,
  output out_3,
  output out_4,
  output out_5,
  output out_6
);

  wire clock_1_out;
  wire [1:0] register_1_q, \下一状态逻辑_1_o2 ;

  \下一状态逻辑  \u_下一状态逻辑_1  (
    .i1(register_1_q[1]), .i2(register_1_q[0]), .IN(in_1), .o1(\下一状态逻辑_1_o2 [1]), .o2(\下一状态逻辑_1_o2 [0]));
  Register #(.width(2)) register_1 (.D(\下一状态逻辑_1_o2 ), .Q(register_1_q), .clk(clock_1_out));  // open: en, clr
  Clock clock_1 (.out(clock_1_out));
  Decoder #(.select(2), .enable("false")) decoder_1 (
    .out0(out_3), .out1(out_4), .out2(out_5), .out3(out_6), .sel(\下一状态逻辑_1_o2 ));

  assign out_2 = 1'b0;
endmodule

module \下一状态逻辑  (
  input  i1,
  input  i2,
  input  IN,
  output o1,
  output o2
);

  wire and_1_out, and_2_out, and_3_out, and_4_out, and_5_out, and_6_out, and_7_out, and_8_out, and_9_out,
       and_10_out, not_1_out, not_2_out, not_3_out, not_4_out, not_5_out, not_6_out, not_7_out, not_8_out,
       or_2_out, or_3_out;

  not not_1 (not_1_out, i1);
  not not_2 (not_2_out, i2);
  not not_3 (not_3_out, i1);
  not not_4 (not_4_out, i2);
  not not_5 (not_5_out, i1);
  not not_6 (not_6_out, i2);
  and and_1 (and_1_out, not_1_out, i2);
  and and_2 (and_2_out, i1, not_2_out);
  and and_3 (and_3_out, not_3_out, not_4_out);
  and and_4 (and_4_out, not_5_out, i2);
  not not_7 (not_7_out, IN);
  and and_5 (and_5_out, i1, not_6_out);
  not not_8 (not_8_out, IN);
  and and_6 (and_6_out, i1, i2);
  or or_1 (o1, and_1_out, and_2_out);
  and and_7 (and_7_out, and_3_out, IN);
  and and_8 (and_8_out, and_4_out, not_7_out);
  and and_9 (and_9_out, and_5_out, not_8_out);
  and and_10 (and_10_out, and_6_out, IN);
  or or_2 (or_2_out, and_7_out, and_8_out);
  or or_3 (or_3_out, and_9_out, and_10_out);
  or or_4 (o2, or_2_out, or_3_out);
endmodule
