// Logisim project 斐波那契数列.circ as structural Verilog: 5 circuits, main circuit main
module main (
  input  [2:0] in_1,
  output [3:0] out_2
);

  wire clock_1_out, comparator_1_eq, comparator_1_gt, comparator_1_lt, or_1_out;
  wire [3:0] multiplexer_1_out, \计算模块_1_out_4 ;

  Clock clock_1 (.out(clock_1_out));
  Comparator #(.width(3), .mode("unsigned")) comparator_1 (
    .a(in_1), .b(3'b001), .gt(comparator_1_gt), .eq(comparator_1_eq), .lt(comparator_1_lt));
  or or_1 (or_1_out, comparator_1_eq, comparator_1_lt);
  \计算模块  \u_计算模块_1  (.CLK(clock_1_out), .\输入数据 (in_1), .\控制按钮 (comparator_1_gt), .out_4(\计算模块_1_out_4 ));
  Multiplexer #(.width(4), .enable("false")) multiplexer_1 (
    .in0(4'b0000), .in1(4'b0001), .out(multiplexer_1_out), .sel(comparator_1_eq));
  Multiplexer #(.width(4), .enable("false")) multiplexer_2 (
    .in0(\计算模块_1_out_4 ), .in1(multiplexer_1_out), .out(out_2), .sel(or_1_out));

  // Notes on the sheet:
  //   接下来的设计思路放在计算函数中
  //   设计思路：首先，通过comparator分离初始值和需要计算才能输出的值
  //   接着，如果是初值1，则输出1，如果不是初值1，则输出0（利用MUX实现）
  //   其次，如果是初值（利用=和<的“或”表示），那么输出它，否则输出计算后的值（利用MUX实现）
  //   回到comparator，如果输入的值大于1，则关于初值的数据通路全部不激活，因此执行计算并输出计算后的值
endmodule

module \计算模块  (
  input  CLK,
  input  [2:0] \输入数据 ,
  input  \控制按钮 ,
  output [3:0] out_4
);

  wire comparator_1_eq, register_1_q;
  wire [2:0] subtractor_1_out;
  wire [3:0] multiplexer_4_out, \矩阵运算_1_a , \矩阵运算_1_b , \矩阵运算_1_c , \矩阵运算_1_d ;
  wire [6:0] multiplexer_2_out, register_2_q, \矩阵运算_1_out_10 ;
  wire [15:0] multiplexer_1_out, multiplexer_3_out, register_3_q;

  Register #(.width(1)) register_1 (.D(1'b1), .Q(register_1_q), .clk(CLK));  // open: en, clr
  Multiplexer #(.width(16), .enable("false")) multiplexer_1 (
    .in0(16'h1110), .in1(register_3_q), .out(multiplexer_1_out), .sel(register_1_q));
  Multiplexer #(.width(7), .enable("false")) multiplexer_2 (
    .in0(7'b0000001), .in1(register_2_q), .out(multiplexer_2_out), .sel(register_1_q));
  Subtractor #(.width(3)) subtractor_1 (.a(\输入数据 ), .b(3'b001), .out(subtractor_1_out));  // open: bin, bout
  \矩阵运算  \u_矩阵运算_1  (
    .preA(multiplexer_1_out[15:12]), .preB(multiplexer_1_out[11:8]), .preC(multiplexer_1_out[7:4]),
    .preD(multiplexer_1_out[3:0]), .in_5(multiplexer_2_out), .A(\矩阵运算_1_a ), .B(\矩阵运算_1_b ), .C(\矩阵运算_1_c ),
    .D(\矩阵运算_1_d ), .out_10(\矩阵运算_1_out_10 ));
  Register #(.width(7)) register_2 (.D(\矩阵运算_1_out_10 ), .Q(register_2_q), .clk(CLK));  // open: en, clr
  Register #(.width(16)) register_3 (
    .D({\矩阵运算_1_a , \矩阵运算_1_b , \矩阵运算_1_c , \矩阵运算_1_d }), .Q(register_3_q), .clk(CLK));  // open: en, clr
  Comparator #(.width(7), .mode("unsigned")) comparator_1 (
    .a(register_2_q), .b({4'b0000, subtractor_1_out}), .eq(comparator_1_eq));  // open: gt, lt
  Multiplexer #(.width(16), .enable("false")) multiplexer_3 (
    .in0({16{1'b0}}), .in1(register_3_q), .out(multiplexer_3_out), .sel(comparator_1_eq));
  Multiplexer #(.width(4), .enable("false")) multiplexer_4 (
    .in0(4'b0000), .in1(multiplexer_3_out[15:12]), .out(multiplexer_4_out), .sel(\控制按钮 ));
  \非0则稳定输出  \u_非0则稳定输出_1  (.in_1(multiplexer_4_out), .CLK(CLK), .out_3(out_4));

  // Notes on the sheet:
  //   矩阵的乘法运算与输出函数分别由两个子模块实现，这里按下不表
  //   本模块有三个输入，即CLK、输入数据、控制按钮，CLK就是时钟周期的接口
  //   设计思路：本模块主要实现的功能是进行斐波那契矩阵的n-1次乘法运算，接着在恰当的时机进行输出
  //   两个子模块，一个成为矩阵运算模块，进行矩阵乘方的运算，另一个成为稳定输出模块，当输入非0时，永远保持此输入
  //   计算结果由输入数据控制输出后，取其最高4位，即为fib[n]，利用控制按钮控制输出，可以看到，如果main中的输入不是至少为2，无论此模块如何运算，其结果也不会被输出
  //   输入数据减1之后（要计算n-1次方，只需进行n-2次矩阵乘法，而运算结果又经过寄存器的一个周期的延时，故减1即可，另外此模块输入数据至少为2，因此不必担心出现负数），成为控制输出的信号
endmodule

module \矩阵运算  (
  input  [3:0] preA,
  input  [3:0] preB,
  input  [3:0] preC,
  input  [3:0] preD,
  input  [6:0] in_5,
  output [3:0] A,
  output [3:0] B,
  output [3:0] C,
  output [3:0] D,
  output [6:0] out_10
);

  Adder #(.width(4)) adder_1 (.a(preA), .b(preB), .out(A));  // open: cin, cout
  Adder #(.width(4)) adder_2 (.a(preC), .b(preD), .out(B));  // open: cin, cout
  Adder #(.width(7)) adder_3 (.a(in_5), .b(7'b0000001), .out(out_10));  // open: cin, cout

  assign C = preA;
  assign D = preC;

  // Notes on the sheet:
  //   本模块旨在实现矩阵乘法，将[[a,b],[c,d]]乘以矩阵[[1,1],[1,0]]，输出结果
endmodule

module \非0则稳定输出  (
  input  [3:0] in_1,
  input  CLK,
  output [3:0] out_3
);

  wire comparator_1_gt;

  Comparator #(.width(4), .mode("unsigned")) comparator_1 (
    .a(in_1), .b(4'b0000), .gt(comparator_1_gt));  // open: eq, lt
  \D锁存器  \d锁存器_1  (.\控制 (comparator_1_gt), .\输入 (in_1), .CLK(CLK), .\输出 (out_3));

  // Notes on the sheet:
  //   本模块旨在实现若输入为非零，则稳定此输入
  //   本模块有两个输入：输入数据、CLK
  //   CLK提供时钟周期，输入数据与comparator比较，得到是否非零的信号，进入D锁存器进行锁存
endmodule

module \D锁存器  (
  input  \控制 ,
  input  [3:0] \输入 ,
  input  CLK,
  output [3:0] \输出 
);

  wire and_1_out, and_2_out, and_3_out, and_4_out, and_5_out, and_6_out, and_7_out, and_8_out,
       multiplexer_1_out, nor_2_out, nor_4_out, nor_6_out, nor_8_out, not_1_out, not_2_out, not_3_out,
       not_4_out, not_5_out, register_1_q;
  wire [3:0] register_2_q;

  Register #(.width(1)) register_1 (.D(1'b1), .en(1'b1), .Q(register_1_q), .clk(CLK));  // open: clr
  Register #(.width(4)) register_2 (.D(\输入 ), .Q(register_2_q), .clk(not_1_out));  // open: en, clr
  not not_1 (not_1_out, CLK);
  Multiplexer #(.enable("false")) multiplexer_1 (.in0(1'b1), .in1(\控制 ), .out(multiplexer_1_out), .sel(register_1_q));
  and and_1 (and_1_out, multiplexer_1_out, not_2_out);
  not not_2 (not_2_out, register_2_q[3]);
  and and_2 (and_2_out, multiplexer_1_out, register_2_q[3]);
  and and_3 (and_3_out, multiplexer_1_out, not_3_out);
  not not_3 (not_3_out, register_2_q[2]);
  and and_4 (and_4_out, multiplexer_1_out, register_2_q[2]);
  and and_5 (and_5_out, multiplexer_1_out, not_4_out);
  not not_4 (not_4_out, register_2_q[1]);
  and and_6 (and_6_out, multiplexer_1_out, register_2_q[1]);
  and and_7 (and_7_out, multiplexer_1_out, not_5_out);
  not not_5 (not_5_out, register_2_q[0]);
  and and_8 (and_8_out, multiplexer_1_out, register_2_q[0]);
  nor nor_1 (\输出 [3], and_1_out, nor_2_out);
  nor nor_2 (nor_2_out, \输出 [3], and_2_out);
  nor nor_3 (\输出 [2], and_3_out, nor_4_out);
  nor nor_4 (nor_4_out, \输出 [2], and_4_out);
  nor nor_5 (\输出 [1], and_5_out, nor_6_out);
  nor nor_6 (nor_6_out, \输出 [1], and_6_out);
  nor nor_7 (\输出 [0], and_7_out, nor_8_out);
  nor nor_8 (nor_8_out, \输出 [0], and_8_out);

  // Notes on the sheet:
  //   本模块有三个接口：控制、输入、CLK
  //   又过半个时钟周期，控制信号关闭，D锁存器锁死，原非零输入数据持续输出
  //   又过半个时钟周期，输入数据归零，但D锁存器已锁死，不影响数据输出
  //   控制信号控制D锁存器工作，当非零信号到达，D锁存器打开，半个时钟周期后，输入数据到达，通过四位锁存器，进行输出
  //   CLK提供时间周期，控制两个装置：一个是控制信号的初始化装置，防止D锁存器出现时序错误，另一个是将输入数据延后半个时钟周期，出于logisim的机制，使控制信号先于输入数据，否则D锁存器无法实现正常功能
endmodule
