// Logisim project 斐波那契数列加强版.circ as structural Verilog: 10 circuits, main circuit main
module main (
  input  [31:0] in_1,
  output [31:0] out_2
);

  wire clock_1_out, comparator_1_eq, comparator_1_gt, comparator_1_lt, or_1_out;
  wire [31:0] multiplexer_1_out, \运算处理_1_输出信号 ;

  Clock clock_1 (.out(clock_1_out));
  Comparator #(.width(32), .mode("unsigned")) comparator_1 (
    .a(in_1), .b(32'h1), .gt(comparator_1_gt), .eq(comparator_1_eq), .lt(comparator_1_lt));
  \运算处理  \u_运算处理_1  (.\输入信号 (in_1), .CLK(clock_1_out), .\控制信号 (comparator_1_gt), .\输出信号 (\运算处理_1_输出信号 ));
  or or_1 (or_1_out, comparator_1_eq, comparator_1_lt);
  Multiplexer #(.width(32), .enable("false")) multiplexer_1 (
    .in0({32{1'b0}}), .in1(32'h1), .out(multiplexer_1_out), .sel(comparator_1_eq));
  Multiplexer #(.width(32), .enable("false")) multiplexer_2 (
    .in0(\运算处理_1_输出信号 ), .in1(multiplexer_1_out), .out(out_2), .sel(or_1_out));
endmodule

module \运算处理  (
  input  [31:0] \输入信号 ,
  input  CLK,
  input  \控制信号 ,
  output [31:0] \输出信号 
);

  wire and_1_out, and_2_out, comparator_1_eq, multiplexer_1_out, \单次触发_1_out_3 ;
  wire [4:0] counter_1_q, register_1_q, register_2_q;
  wire [31:0] multiplexer_2_out, \矩阵快速幂_1_a , \矩阵快速幂_1_b , \矩阵快速幂_1_c , \矩阵快速幂_1_d , \累乘输出_1_out_7 ;

  Counter #(.width(5), .max('h1f)) counter_1 (.Q(counter_1_q), .clk(CLK));  // open: load, D, count, carry, clr
  Multiplexer #(.select(5), .enable("false")) multiplexer_1 (
    .in0(\输入信号 [0]), .in1(\输入信号 [1]), .in2(\输入信号 [2]), .in3(\输入信号 [3]), .in4(\输入信号 [4]), .in5(\输入信号 [5]),
    .in6(\输入信号 [6]), .in7(\输入信号 [7]), .in8(\输入信号 [8]), .in9(\输入信号 [9]), .in10(\输入信号 [10]), .in11(\输入信号 [11]),
    .in12(\输入信号 [12]), .in13(\输入信号 [13]), .in14(\输入信号 [14]), .in15(\输入信号 [15]), .in16(\输入信号 [16]),
    .in17(\输入信号 [17]), .in18(\输入信号 [18]), .in19(\输入信号 [19]), .in20(\输入信号 [20]), .in21(\输入信号 [21]),
    .in22(\输入信号 [22]), .in23(\输入信号 [23]), .in24(\输入信号 [24]), .in25(\输入信号 [25]), .in26(\输入信号 [26]),
    .in27(\输入信号 [27]), .in28(\输入信号 [28]), .in29(\输入信号 [29]), .in30(\输入信号 [30]), .in31(\输入信号 [31]),
    .out(multiplexer_1_out), .sel(counter_1_q));
  Register #(.width(5)) register_1 (.D(counter_1_q), .Q(register_1_q), .clk(CLK));  // open: en, clr
  \矩阵快速幂  \u_矩阵快速幂_1  (
    .\当前位 (multiplexer_1_out), .CLK(CLK), .A(\矩阵快速幂_1_a ), .B(\矩阵快速幂_1_b ), .C(\矩阵快速幂_1_c ), .D(\矩阵快速幂_1_d ));
  Register #(.width(5)) register_2 (.D(register_1_q), .Q(register_2_q), .clk(CLK));  // open: en, clr
  \单次触发  \u_单次触发_1  (.in_1(comparator_1_eq), .CLK(CLK), .out_3(\单次触发_1_out_3 ));
  \累乘输出  \u_累乘输出_1  (
    .in_1(\矩阵快速幂_1_a ), .in_2(\矩阵快速幂_1_b ), .in_3(\矩阵快速幂_1_c ), .in_4(\矩阵快速幂_1_d ), .CLK(CLK),
    .out_7(\累乘输出_1_out_7 ));  // open: out_6, out_8, out_9
  and and_1 (and_1_out, \控制信号 , \单次触发_1_out_3 );
  Comparator #(.width(5), .mode("unsigned")) comparator_1 (
    .a({5{1'b1}}), .b(register_2_q), .eq(comparator_1_eq));  // open: gt, lt
  and and_2 (and_2_out, comparator_1_eq, and_1_out);
  Multiplexer #(.width(32), .enable("false")) multiplexer_2 (
    .in0({32{1'b0}}), .in1(\累乘输出_1_out_7 ), .out(multiplexer_2_out), .sel(and_2_out));
  \稳定输出  \u_稳定输出_1  (.in_1(multiplexer_2_out), .CLK(CLK), .out_3(\输出信号 ));
endmodule

module \矩阵快速幂  (
  input  \当前位 ,
  input  CLK,
  output [31:0] A,
  output [31:0] B,
  output [31:0] C,
  output [31:0] D
);

  wire [31:0] fib_2_1_out_2, fib_2_1_out_3, fib_2_1_out_4, fib_2_1_out_5;

  fib_2 fib_2_1 (.CLK(CLK), .out_2(fib_2_1_out_2), .out_3(fib_2_1_out_3), .out_4(fib_2_1_out_4), .out_5(fib_2_1_out_5));
  Multiplexer #(.width(32), .enable("false")) multiplexer_1 (.in0(32'h1), .in1(fib_2_1_out_2), .out(A), .sel(\当前位 ));
  Multiplexer #(.width(32), .enable("false")) multiplexer_2 (
    .in0({32{1'b0}}), .in1(fib_2_1_out_3), .out(B), .sel(\当前位 ));
  Multiplexer #(.width(32), .enable("false")) multiplexer_3 (
    .in0({32{1'b0}}), .in1(fib_2_1_out_4), .out(C), .sel(\当前位 ));
  Multiplexer #(.width(32), .enable("false")) multiplexer_4 (.in0(32'h1), .in1(fib_2_1_out_5), .out(D), .sel(\当前位 ));

  // Notes on the sheet:
  //   输入当前位，1则输出当前矩阵幂，0则输出单位矩阵
endmodule

module \累乘输出  (
  input  [31:0] in_1,
  input  [31:0] in_2,
  input  [31:0] in_3,
  input  [31:0] in_4,
  input  CLK,
  output [31:0] out_6,
  output [31:0] out_7,
  output [31:0] out_8,
  output [31:0] out_9
);

  wire register_5_q, register_6_q, register_7_q, register_8_q;
  wire [31:0] multiplexer_1_out, multiplexer_2_out, multiplexer_3_out, multiplexer_4_out, register_1_q,
       register_2_q, register_3_q, register_4_q, \矩阵相乘_1_a , \矩阵相乘_1_b , \矩阵相乘_1_c , \矩阵相乘_1_d ;

  Register #(.width(32)) register_1 (.D(in_1), .Q(register_1_q), .clk(CLK));  // open: en, clr
  Register #(.width(32)) register_2 (.D(in_2), .Q(register_2_q), .clk(CLK));  // open: en, clr
  Register #(.width(32)) register_3 (.D(in_3), .Q(register_3_q), .clk(CLK));  // open: en, clr
  Register #(.width(32)) register_4 (.D(in_4), .Q(register_4_q), .clk(CLK));  // open: en, clr
  Multiplexer #(.width(32), .enable("false")) multiplexer_1 (
    .in0(32'h1), .in1(register_1_q), .out(multiplexer_1_out), .sel(register_5_q));
  Register #(.width(1)) register_5 (.D(1'b1), .Q(register_5_q), .clk(CLK));  // open: en, clr
  Multiplexer #(.width(32), .enable("false")) multiplexer_2 (
    .in0({32{1'b0}}), .in1(register_2_q), .out(multiplexer_2_out), .sel(register_6_q));
  Register #(.width(1)) register_6 (.D(1'b1), .Q(register_6_q), .clk(CLK));  // open: en, clr
  Multiplexer #(.width(32), .enable("false")) multiplexer_3 (
    .in0({32{1'b0}}), .in1(register_3_q), .out(multiplexer_3_out), .sel(register_7_q));
  Register #(.width(1)) register_7 (.D(1'b1), .Q(register_7_q), .clk(CLK));  // open: en, clr
  Multiplexer #(.width(32), .enable("false")) multiplexer_4 (
    .in0(32'h1), .in1(register_4_q), .out(multiplexer_4_out), .sel(register_8_q));
  Register #(.width(1)) register_8 (.D(1'b1), .Q(register_8_q), .clk(CLK));  // open: en, clr
  \矩阵相乘  \u_矩阵相乘_1  (
    .a1(out_6), .b1(out_7), .c1(out_8), .d1(out_9), .a2(multiplexer_1_out), .b2(multiplexer_2_out),
    .c2(multiplexer_3_out), .d2(multiplexer_4_out), .CLK(CLK), .a(\矩阵相乘_1_a ), .b(\矩阵相乘_1_b ),
    .c(\矩阵相乘_1_c ), .d(\矩阵相乘_1_d ));
  Register #(.width(32)) register_9 (.D(\矩阵相乘_1_a ), .Q(out_6), .clk(CLK));  // open: en, clr
  Register #(.width(32)) register_10 (.D(\矩阵相乘_1_b ), .Q(out_7), .clk(CLK));  // open: en, clr
  Register #(.width(32)) register_11 (.D(\矩阵相乘_1_c ), .Q(out_8), .clk(CLK));  // open: en, clr
  Register #(.width(32)) register_12 (.D(\矩阵相乘_1_d ), .Q(out_9), .clk(CLK));  // open: en, clr

  // Notes on the sheet:
  //   初始锁存单位矩阵，第n个上升沿后输出第n-2位及之前乘积的结果
  //   即，第2个上升沿后，输出第0位的矩阵幂结果；第3个上升沿后，输出第1位矩阵幂及之前（只有第0位）的结果的乘积
endmodule

module \稳定输出  (
  input  [31:0] in_1,
  input  CLK,
  output [31:0] out_3
);

  wire comparator_1_gt;

  Comparator #(.width(32), .mode("unsigned")) comparator_1 (
    .a(in_1), .b({32{1'b0}}), .gt(comparator_1_gt));  // open: eq, lt
  \_32位锁存器  \u_32位锁存器_1  (.\控制 (comparator_1_gt), .\输入 (in_1), .CLK(CLK), .out_4(out_3));

  // Notes on the sheet:
  //   输入非零则稳定输出
endmodule

module fib_2 (
  input  CLK,
  output [31:0] out_2,
  output [31:0] out_3,
  output [31:0] out_4,
  output [31:0] out_5
);

  wire register_5_q, register_6_q, register_7_q, register_8_q;
  wire [31:0] register_1_q, register_2_q, register_3_q, register_4_q, \矩阵幂乘_1_a , \矩阵幂乘_1_b , \矩阵幂乘_1_c ,
       \矩阵幂乘_1_d ;

  Register #(.width(32)) register_1 (.D(out_2), .Q(register_1_q), .clk(CLK));  // open: en, clr
  Register #(.width(32)) register_2 (.D(out_3), .Q(register_2_q), .clk(CLK));  // open: en, clr
  Register #(.width(32)) register_3 (.D(out_4), .Q(register_3_q), .clk(CLK));  // open: en, clr
  Register #(.width(32)) register_4 (.D(out_5), .Q(register_4_q), .clk(CLK));  // open: en, clr
  \矩阵幂乘  \u_矩阵幂乘_1  (
    .preA(register_1_q), .preB(register_2_q), .preC(register_3_q), .preD(register_4_q), .A(\矩阵幂乘_1_a ),
    .B(\矩阵幂乘_1_b ), .C(\矩阵幂乘_1_c ), .D(\矩阵幂乘_1_d ));
  Register #(.width(1)) register_5 (.D(1'b1), .Q(register_5_q), .clk(CLK));  // open: en, clr
  Register #(.width(1)) register_6 (.D(1'b1), .Q(register_6_q), .clk(CLK));  // open: en, clr
  Register #(.width(1)) register_7 (.D(1'b1), .Q(register_7_q), .clk(CLK));  // open: en, clr
  Register #(.width(1)) register_8 (.D(1'b1), .Q(register_8_q), .clk(CLK));  // open: en, clr
  Multiplexer #(.width(32), .enable("false")) multiplexer_1 (
    .in0(32'h1), .in1(\矩阵幂乘_1_a ), .out(out_2), .sel(register_5_q));
  Multiplexer #(.width(32), .enable("false")) multiplexer_2 (
    .in0(32'h1), .in1(\矩阵幂乘_1_b ), .out(out_3), .sel(register_6_q));
  Multiplexer #(.width(32), .enable("false")) multiplexer_3 (
    .in0(32'h1), .in1(\矩阵幂乘_1_c ), .out(out_4), .sel(register_7_q));
  Multiplexer #(.width(32), .enable("false")) multiplexer_4 (
    .in0({32{1'b0}}), .in1(\矩阵幂乘_1_d ), .out(out_5), .sel(register_8_q));

  // Notes on the sheet:
  //   初始输出1110，第n个时钟上升沿输出1110^(2^n)
endmodule

module \矩阵幂乘  (
  input  [31:0] preA,
  input  [31:0] preB,
  input  [31:0] preC,
  input  [31:0] preD,
  output [31:0] A,
  output [31:0] B,
  output [31:0] C,
  output [31:0] D
);

  wire [31:0] multiplier_1_out, multiplier_2_out, multiplier_3_out, multiplier_4_out, multiplier_5_out,
       multiplier_6_out, multiplier_7_out, multiplier_8_out;

  Multiplier #(.width(32)) multiplier_1 (.a(preA), .b(preA), .out(multiplier_1_out));  // open: cin, cout
  Multiplier #(.width(32)) multiplier_2 (.a(preB), .b(preC), .out(multiplier_2_out));  // open: cin, cout
  Multiplier #(.width(32)) multiplier_3 (.a(preA), .b(preB), .out(multiplier_3_out));  // open: cin, cout
  Multiplier #(.width(32)) multiplier_4 (.a(preB), .b(preD), .out(multiplier_4_out));  // open: cin, cout
  Multiplier #(.width(32)) multiplier_5 (.a(preA), .b(preC), .out(multiplier_5_out));  // open: cin, cout
  Multiplier #(.width(32)) multiplier_6 (.a(preC), .b(preD), .out(multiplier_6_out));  // open: cin, cout
  Multiplier #(.width(32)) multiplier_7 (.a(preB), .b(preC), .out(multiplier_7_out));  // open: cin, cout
  Multiplier #(.width(32)) multiplier_8 (.a(preD), .b(preD), .out(multiplier_8_out));  // open: cin, cout
  Adder #(.width(32)) adder_1 (.a(multiplier_1_out), .b(multiplier_2_out), .out(A));  // open: cin, cout
  Adder #(.width(32)) adder_2 (.a(multiplier_3_out), .b(multiplier_4_out), .out(B));  // open: cin, cout
  Adder #(.width(32)) adder_3 (.a(multiplier_5_out), .b(multiplier_6_out), .out(C));  // open: cin, cout
  Adder #(.width(32)) adder_4 (.a(multiplier_7_out), .b(multiplier_8_out), .out(D));  // open: cin, cout

  // Notes on the sheet:
  //   矩阵自乘
endmodule

module \矩阵相乘  (
  input  [31:0] a1,
  input  [31:0] b1,
  input  [31:0] c1,
  input  [31:0] d1,
  input  [31:0] a2,
  input  [31:0] b2,
  input  [31:0] c2,
  input  [31:0] d2,
  input  CLK,
  output [31:0] a,
  output [31:0] b,
  output [31:0] c,
  output [31:0] d
);

  wire register_1_q;
  wire [31:0] multiplexer_1_out, multiplexer_2_out, multiplexer_3_out, multiplexer_4_out, multiplier_1_out,
       multiplier_2_out, multiplier_3_out, multiplier_4_out, multiplier_5_out, multiplier_6_out,
       multiplier_7_out, multiplier_8_out;

  Register #(.width(1)) register_1 (.D(1'b1), .Q(register_1_q), .clk(CLK));  // open: en, clr
  Multiplexer #(.width(32), .enable("false")) multiplexer_1 (
    .in0(32'h1), .in1(a1), .out(multiplexer_1_out), .sel(register_1_q));
  Multiplexer #(.width(32), .enable("false")) multiplexer_2 (
    .in0({32{1'b0}}), .in1(b1), .out(multiplexer_2_out), .sel(register_1_q));
  Multiplexer #(.width(32), .enable("false")) multiplexer_3 (
    .in0({32{1'b0}}), .in1(c1), .out(multiplexer_3_out), .sel(register_1_q));
  Multiplexer #(.width(32), .enable("false")) multiplexer_4 (
    .in0(32'h1), .in1(d1), .out(multiplexer_4_out), .sel(register_1_q));
  Multiplier #(.width(32)) multiplier_1 (.a(multiplexer_1_out), .b(a2), .out(multiplier_1_out));  // open: cin, cout
  Multiplier #(.width(32)) multiplier_2 (.a(multiplexer_2_out), .b(c2), .out(multiplier_2_out));  // open: cin, cout
  Multiplier #(.width(32)) multiplier_3 (.a(multiplexer_1_out), .b(b2), .out(multiplier_3_out));  // open: cin, cout
  Multiplier #(.width(32)) multiplier_4 (.a(multiplexer_2_out), .b(d2), .out(multiplier_4_out));  // open: cin, cout
  Multiplier #(.width(32)) multiplier_5 (.a(multiplexer_3_out), .b(a2), .out(multiplier_5_out));  // open: cin, cout
  Multiplier #(.width(32)) multiplier_6 (.a(multiplexer_4_out), .b(c2), .out(multiplier_6_out));  // open: cin, cout
  Multiplier #(.width(32)) multiplier_7 (.a(multiplexer_3_out), .b(b2), .out(multiplier_7_out));  // open: cin, cout
  Multiplier #(.width(32)) multiplier_8 (.a(multiplexer_4_out), .b(d2), .out(multiplier_8_out));  // open: cin, cout
  Adder #(.width(32)) adder_1 (.a(multiplier_1_out), .b(multiplier_2_out), .out(a));  // open: cin, cout
  Adder #(.width(32)) adder_2 (.a(multiplier_3_out), .b(multiplier_4_out), .out(b));  // open: cin, cout
  Adder #(.width(32)) adder_3 (.a(multiplier_5_out), .b(multiplier_6_out), .out(c));  // open: cin, cout
  Adder #(.width(32)) adder_4 (.a(multiplier_7_out), .b(multiplier_8_out), .out(d));  // open: cin, cout
endmodule

module \单次触发  (
  input  in_1,
  input  CLK,
  output out_3
);

  wire not_1_out, not_2_out, register_1_q, register_2_q;

  not not_1 (not_1_out, CLK);
  Register #(.width(1)) register_1 (.D(in_1), .Q(register_1_q), .clk(not_1_out));  // open: en, clr
  not not_2 (not_2_out, register_2_q);
  Register #(.width(1)) register_2 (.D(1'b1), .Q(register_2_q), .clk(register_1_q));  // open: en, clr
  Register #(.width(1)) register_3 (.D(not_2_out), .Q(out_3), .clk(CLK));  // open: en, clr

  // Notes on the sheet:
  //   实现功能：控制信号变为1时，输出不会立刻变为0，而是等到下一个时钟上升沿后才变为0
  //   上方控制信号较下方时钟信号要经过多个组合逻辑模块，所以较慢，功能可行
  //   具体来说，CLK变为1时，控制信号仍为0，输出仍为1；CLk再一次处于1时，控制信号仍处于1而未变为0，故输出0
endmodule

module \_32位锁存器  (
  input  \控制 ,
  input  [31:0] \输入 ,
  input  CLK,
  output [31:0] out_4
);

  wire multiplexer_1_out, not_1_out, register_1_q;
  wire [31:0] register_2_q;

  Register #(.width(1)) register_1 (.D(1'b1), .Q(register_1_q), .clk(CLK));  // open: en, clr
  Register #(.width(32)) register_2 (.D(\输入 ), .Q(register_2_q), .clk(not_1_out));  // open: en, clr
  not not_1 (not_1_out, CLK);
  Multiplexer #(.enable("false")) multiplexer_1 (.in0(1'b1), .in1(\控制 ), .out(multiplexer_1_out), .sel(register_1_q));
  Register #(.width(32)) register_3 (.D(register_2_q), .en(multiplexer_1_out), .Q(out_4), .clk(CLK));  // open: clr
endmodule
